// Logisim project BCD_Decimal.circ as structural Verilog: 9 circuits, main circuit main
module main (
  input  in_1,
  input  in_2,
  input  in_3,
  input  in_4,
  input  in_5,
  input  in_6,
  input  in_7,
  input  in_8,
  input  in_9
);

  wire a_1_out_5, b_1_out_5, c_1_out_5, d_1_out_5, d_ff_1_out_3, d_ff_2_out_3, d_ff_3_out_3, d_ff_4_out_3,
       e_1_out_5, f_1_out_5, g_1_out_5, or_1_out, or_2_out, or_3_out, or_4_out, or_5_out;

  or or_1 (or_1_out, in_1, in_3, in_5, in_7, in_9);
  or or_2 (or_2_out, in_2, in_3, in_6, in_7);
  or or_3 (or_3_out, in_4, in_5, in_6, in_7);
  or or_4 (or_4_out, in_8, in_9);
  or or_5 (or_5_out, in_1, in_2, in_3, in_4, in_5, in_6, in_7, in_8, in_9);
  D_FF d_ff_1 (.D(or_1_out), .C(or_5_out), .out_3(d_ff_1_out_3));
  D_FF d_ff_2 (.D(or_2_out), .C(or_5_out), .out_3(d_ff_2_out_3));
  D_FF d_ff_3 (.D(or_3_out), .C(or_5_out), .out_3(d_ff_3_out_3));
  D_FF d_ff_4 (.D(or_4_out), .C(or_5_out), .out_3(d_ff_4_out_3));
  A a_1 (.A(d_ff_1_out_3), .B(d_ff_2_out_3), .C(d_ff_3_out_3), .D(d_ff_4_out_3), .out_5(a_1_out_5));
  B b_1 (.A(d_ff_1_out_3), .B(d_ff_2_out_3), .C(d_ff_3_out_3), .D(d_ff_4_out_3), .out_5(b_1_out_5));
  C c_1 (.A(d_ff_1_out_3), .B(d_ff_2_out_3), .C(d_ff_3_out_3), .D(d_ff_4_out_3), .out_5(c_1_out_5));
  D d_1 (.A(d_ff_1_out_3), .B(d_ff_2_out_3), .C(d_ff_3_out_3), .D(d_ff_4_out_3), .out_5(d_1_out_5));
  E e_1 (.A(d_ff_1_out_3), .B(d_ff_2_out_3), .C(d_ff_3_out_3), .D(d_ff_4_out_3), .out_5(e_1_out_5));
  F f_1 (.A(d_ff_1_out_3), .B(d_ff_2_out_3), .C(d_ff_3_out_3), .D(d_ff_4_out_3), .out_5(f_1_out_5));
  G g_1 (.A(d_ff_1_out_3), .B(d_ff_2_out_3), .C(d_ff_3_out_3), .D(d_ff_4_out_3), .out_5(g_1_out_5));
  _7_Segment_Display u_7_segment_display_1 (
    .g(g_1_out_5), .f(f_1_out_5), .a(a_1_out_5), .b(b_1_out_5), .e(e_1_out_5), .d(d_1_out_5), .c(c_1_out_5));  // open: dp

  // Notes on the sheet:
  //   1
  //   2
  //   3
  //   4
  //   5
  //   6
  //   8
  //   7
  //   9
  //   A
  //   B
  //   C
  //   D
endmodule

module A (
  input  A,
  input  B,
  input  C,
  input  D,
  output out_5
);

  wire and_1_out, and_2_out, not_1_out, not_2_out, not_3_out, not_4_out;

  not not_1 (not_1_out, B);
  and and_1 (and_1_out, A, not_1_out, C);
  not not_2 (not_2_out, A);
  not not_3 (not_3_out, B);
  and and_2 (and_2_out, not_2_out, not_3_out, not_4_out);
  not not_4 (not_4_out, C);
  or or_1 (out_5, and_1_out, B, and_2_out, D);
endmodule

module B (
  input  A,
  input  B,
  input  C,
  input  D,
  output out_5
);

  wire and_1_out, and_2_out, and_3_out, and_4_out, not_1_out, not_2_out, not_3_out, not_4_out, not_5_out,
       not_6_out;

  not not_1 (not_1_out, B);
  not not_2 (not_2_out, A);
  not not_3 (not_3_out, B);
  not not_4 (not_4_out, D);
  not not_5 (not_5_out, C);
  not not_6 (not_6_out, D);
  and and_1 (and_1_out, not_2_out, not_3_out);
  and and_2 (and_2_out, A, B, not_4_out);
  and and_3 (and_3_out, not_5_out, not_6_out);
  and and_4 (and_4_out, A, not_1_out, not_5_out);
  or or_1 (out_5, and_1_out, and_2_out, and_3_out, and_4_out);
endmodule

module C (
  input  A,
  input  B,
  input  C,
  input  D,
  output out_5
);

  wire and_1_out, not_1_out, not_2_out;

  not not_1 (not_1_out, D);
  and and_1 (and_1_out, B, C, not_1_out);
  not not_2 (not_2_out, B);
  or or_1 (out_5, A, not_2_out, and_1_out);
endmodule

module D (
  input  A,
  input  B,
  input  C,
  input  D,
  output out_5
);

  wire and_1_out, and_2_out, and_3_out, and_4_out, and_5_out, not_1_out, not_2_out, not_3_out, not_4_out,
       not_5_out, not_6_out;

  not not_1 (not_1_out, C);
  not not_2 (not_2_out, A);
  not not_3 (not_3_out, B);
  not not_4 (not_4_out, A);
  and and_1 (and_1_out, not_4_out, B);
  and and_2 (and_2_out, B, not_5_out);
  not not_5 (not_5_out, C);
  not not_6 (not_6_out, B);
  and and_3 (and_3_out, not_6_out, D);
  and and_4 (and_4_out, not_2_out, not_3_out, not_1_out);
  and and_5 (and_5_out, A, not_3_out, C);
  or or_1 (out_5, and_1_out, and_2_out, and_3_out, and_4_out, and_5_out);
endmodule

module E (
  input  A,
  input  B,
  input  C,
  input  D,
  output out_5
);

  wire and_1_out, and_2_out, and_3_out, not_1_out, not_2_out;

  not not_1 (not_1_out, A);
  not not_2 (not_2_out, C);
  and and_1 (and_1_out, not_1_out, not_2_out);
  and and_2 (and_2_out, B, not_1_out);
  and and_3 (and_3_out, not_1_out, not_2_out, D);
  or or_1 (out_5, and_1_out, and_2_out, and_3_out);
endmodule

module F (
  input  A,
  input  B,
  input  C,
  input  D,
  output out_5
);

  wire and_1_out, and_2_out, and_3_out, and_4_out, not_1_out, not_2_out, not_3_out;

  not not_1 (not_1_out, A);
  not not_2 (not_2_out, B);
  not not_3 (not_3_out, C);
  and and_1 (and_1_out, not_1_out, not_2_out);
  and and_2 (and_2_out, not_1_out, B, C);
  and and_3 (and_3_out, A, not_2_out, C);
  and and_4 (and_4_out, A, not_2_out, not_3_out, D);
  or or_1 (out_5, and_1_out, and_2_out, and_3_out, and_4_out);
endmodule

module G (
  input  A,
  input  B,
  input  C,
  input  D,
  output out_5
);

  wire and_1_out, and_2_out, and_3_out, and_4_out, not_1_out, not_2_out, not_3_out, not_4_out, not_5_out,
       not_6_out;

  not not_1 (not_1_out, A);
  not not_2 (not_2_out, B);
  not not_3 (not_3_out, C);
  not not_4 (not_4_out, D);
  not not_5 (not_5_out, C);
  and and_1 (and_1_out, not_1_out, B);
  and and_2 (and_2_out, not_2_out, C);
  and and_3 (and_3_out, B, not_3_out, not_4_out);
  not not_6 (not_6_out, B);
  and and_4 (and_4_out, not_6_out, not_5_out, D);
  or or_1 (out_5, and_1_out, and_2_out, and_3_out, and_4_out);
endmodule

module D_FF (
  input  D,
  input  C,
  output out_3
);

  wire nand_1_out, nand_2_out, nand_4_out, not_1_out;

  not not_1 (not_1_out, D);
  nand nand_1 (nand_1_out, D, C);
  nand nand_2 (nand_2_out, C, not_1_out);
  nand nand_3 (out_3, nand_1_out, nand_4_out);
  nand nand_4 (nand_4_out, out_3, nand_2_out);
endmodule
