// Logisim project Sync_Counter.circ as structural Verilog: 9 circuits, main circuit main
module main (
);

  wire cod_1_out_3, cod_1_out_4, cod_1_out_5, cod_1_out_6, cod_1_out_7, cod_1_out_8, d_ff_1_q, d_ff_1_qn,
       d_ff_2_q, switch_1_p2, xor_1_out;

  LED led_1 (.in(switch_1_p2));
  // Switch switch_1: pin names not known; wires that end beside it: 1'b1, switch_1_p2
  Pull_Resistor pull_resistor_1 (.node(switch_1_p2));
  xor xor_1 (xor_1_out, d_ff_1_q, d_ff_2_q);
  D_Flip_Flop d_ff_1 (.D(d_ff_1_qn), .clk(switch_1_p2), .Q(d_ff_1_q), .Qn(d_ff_1_qn), .preset(1'b0), .reset(1'b0));
  D_Flip_Flop d_ff_2 (.D(xor_1_out), .clk(switch_1_p2), .Q(d_ff_2_q), .preset(1'b0), .reset(1'b0));  // open: Qn
  COD cod_1 (
    .in_1(d_ff_1_q), .in_2(d_ff_2_q), .out_3(cod_1_out_3), .out_4(cod_1_out_4), .out_5(cod_1_out_5),
    .out_6(cod_1_out_6), .out_7(cod_1_out_7), .out_8(cod_1_out_8));
  _7_Segment_Display u_7_segment_display_1 (
    .g(cod_1_out_8), .f(cod_1_out_7), .a(cod_1_out_3), .b(cod_1_out_4), .e(cod_1_out_6), .d(cod_1_out_3),
    .c(cod_1_out_5));  // open: dp
endmodule

module A (
  input  Q0,
  input  Q1,
  output out_3
);

  wire and_1_out, and_2_out, and_3_out, not_1_out, not_2_out, not_3_out;

  not not_1 (not_1_out, Q0);
  not not_2 (not_2_out, Q1);
  not not_3 (not_3_out, Q0);
  and and_1 (and_1_out, not_1_out, not_2_out);
  and and_2 (and_2_out, not_3_out, Q1);
  and and_3 (and_3_out, Q0, Q1);
  or or_1 (out_3, and_1_out, and_2_out, and_3_out);
endmodule

module B (
  input  Q0,
  input  Q1,
  output out_3
);

  wire and_1_out, not_1_out, not_2_out, or_1_out;

  not not_1 (not_1_out, Q0);
  not not_2 (not_2_out, Q1);
  and and_1 (and_1_out, not_1_out, not_2_out);
  or or_1 (or_1_out, Q0, Q1);
  or or_2 (out_3, and_1_out, or_1_out);
endmodule

module C (
  input  Q0,
  input  Q1,
  output out_3
);

  wire and_1_out, and_2_out, and_3_out, not_1_out, not_2_out, not_3_out;

  not not_1 (not_1_out, Q0);
  not not_2 (not_2_out, Q1);
  not not_3 (not_3_out, Q1);
  and and_1 (and_1_out, not_1_out, not_2_out);
  and and_2 (and_2_out, Q0, not_3_out);
  and and_3 (and_3_out, Q0, Q1);
  or or_1 (out_3, and_1_out, and_2_out, and_3_out);
endmodule

module E (
  input  Q0,
  output out_2
);

  not not_1 (out_2, Q0);
endmodule

module F (
  input  Q0,
  input  Q1,
  output out_3
);

  wire not_1_out, not_2_out;

  not not_1 (not_1_out, Q0);
  not not_2 (not_2_out, Q1);
  and and_1 (out_3, not_1_out, not_2_out);
endmodule

module G (
  input  Q1,
  output out_2
);


  assign out_2 = Q1;
endmodule

module h (
  input  Q0,
  input  Q1,
  output out_3
);

  wire and_1_out, and_2_out, not_1_out, not_2_out;

  not not_1 (not_1_out, Q0);
  not not_2 (not_2_out, Q1);
  and and_1 (and_1_out, not_1_out, not_2_out);
  and and_2 (and_2_out, Q0, Q1);
  or or_1 (out_3, and_1_out, and_2_out);
endmodule

module COD (
  input  in_1,
  input  in_2,
  output out_3,
  output out_4,
  output out_5,
  output out_6,
  output out_7,
  output out_8
);

  A a_1 (.Q0(in_1), .Q1(in_2), .out_3(out_3));
  B b_1 (.Q0(in_1), .Q1(in_2), .out_3(out_4));
  C c_1 (.Q0(in_1), .Q1(in_2), .out_3(out_5));
  E e_1 (.Q0(in_1), .out_2(out_6));
  F f_1 (.Q0(in_1), .Q1(in_2), .out_3(out_7));
  G g_1 (.Q1(in_2), .out_2(out_8));
endmodule
